# Fritzing sketch Layout (saved by Fritzing 0.9.3b)
breadboards: 1

parts:
  Aduino_Uno_SMD_with_CH340G_(Chinese) = Arduino Uno (Rev3) - ICSP
  Ethernet_Shield_W5100 = Arduino Ethernet Shield (Rev3)
  Part1 = Adafruit TSL2561 [part_number="Adafruit #439"]  # not connected
  DHT1 = DHT22 Humidity and Temperature Sensor  # not connected

nets:
  5V: Aduino_Uno_SMD_with_CH340G_(Chinese).5V, Ethernet_Shield_W5100.5V
  N1: Aduino_Uno_SMD_with_CH340G_(Chinese).ICSP_MOSI, Aduino_Uno_SMD_with_CH340G_(Chinese).D11_PWM/MOSI, Ethernet_Shield_W5100.PWM_D11
  N2: Aduino_Uno_SMD_with_CH340G_(Chinese).D10_PWM/SS, Ethernet_Shield_W5100.ETH_CS
  N3: Aduino_Uno_SMD_with_CH340G_(Chinese).D12/MISO, Ethernet_Shield_W5100.SPI/D12
  N4: Aduino_Uno_SMD_with_CH340G_(Chinese).D13/SCK, Ethernet_Shield_W5100.SPI/D13
  GND: Aduino_Uno_SMD_with_CH340G_(Chinese).GND, Ethernet_Shield_W5100.GND
  N5: Aduino_Uno_SMD_with_CH340G_(Chinese).D4, Ethernet_Shield_W5100.SDCS

notes:
  References:
  - Ethernet Shield W5100: https://radiomart.kz/analogi-arduino-kitaj/414-ethernet-shield-w5100-8543708000.html
  - Aduino Uno SMD with CH340G (Chinese): https://radiomart.kz/analogi-arduino-kitaj/1006-aduino-uno-smd-na-ch340g-kitaj-8543708000.html
  - DHT22 (AM2302): https://radiomart.kz/datchiki-temperatury/493-datchik-temperatury-i-vlazhnosti-dht22-9031803800.html
  -GY-2561 (TSL2561): https://radiomart.kz/datchiki-sveta-ognya/6160-cifrovoj-datchik-urovnya-osvesshennosti-gy-2561-tsl2561.html

custom parts:
  Adafruit TSL2561: The TSL2561 luminosity sensor is an advanced digital light sensor, ideal for use in a wide range of light situations. Compared to low cost CdS cells, this sensor is more precise, allowing for exact lux calculations and can be configured for different gain/timing ranges to detect light ranges from up to 0.1 - 40,000+ Lux on the fly. The best part of this sensor is that it contains both infrared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
